# Fritzing sketch sunset (saved by Fritzing 1.0.1rc)
breadboards: 1

parts:
  U1 = 555 Timer [package="DIP8 [THT]"]
  C1 = Capacitor Polarized [package=cpol-radial-100uf-25v]
  LED1 = smd LED [color="Red (633nm)" package="0805 [SMD]"]
  LED2 = smd LED [color="Red (633nm)" package="0805 [SMD]"]
  R1 = Resistor [tolerance=±5% resistance=220 package="0603 [SMD]"]
  R2 = Resistor [tolerance=±5% resistance=220 package="0603 [SMD]"]
  S1 = Toggle Switch [package=THT]
  R3 = Resistor [tolerance=±5% resistance=220 package="0603 [SMD]"]

nets (from the breadboard view):
  N1: U1.Ground, C1.-, R2.Pin_1, S1.COM
  N2: U1.Trigger, U1.Threshold, C1.+, R1.Pin_0
  N3: U1.Output, LED1.cathode, LED2.cathode
  N4: U1.Reset, U1.Vcc_Supply_Voltage
  N5: U1.Discharge, R1.Pin_1, R3.Pin_1
  N6: LED1.anode, LED2.anode, R2.Pin_0

notes:
  Postive 5V
  Ground
